# Fritzing sketch V1 (saved by Fritzing 0.8.7b)
breadboards: 1

parts:
  Power_plug1 = Power plug
  Part1 = Arduino Uno (Rev3)
  S1 = Pushbutton [package="[THT]"]
  R1 = Resistor [tolerance=±5% resistance=220 package=THT]
  Q1 = Basic FET P-Channel [package="TO220 [THT]"]
  R2 = Resistor [tolerance=±5% resistance=1.5k package=THT]
  D1 = Rectifier Diode [part_number=1N4001 package="300 mil [THT]"]
  L1 = Solenoid

nets:
  GND: Power_plug1.GND, Part1.GND, R1.Pin_0, Q1.gate
  N1: Power_plug1.VCC, D1.cathode, L1.pin2
  N2: Part1.D2, R2.Pin_1
  N3: Part1.D7, S1.Pin_3, S1.Pin_4, R1.Pin_1
  N4: Part1.3V3, S1.Pin_1, S1.Pin_2
  N5: Q1.drain, D1.anode, L1.pin1
  N6: Q1.source, R2.Pin_0
